# Fritzing sketch OhmMeter Sketch (saved by Fritzing 0.9.4)
breadboards: 1

parts:
  Part1 = Arduino Uno (Rev3) - ICSP
  R1 = Rotary Potentiometer (Small) [maximum_resistance=100kΩ package=THT]
  R2 = Resistor [tolerance=±5% resistance=220 package=THT]
  Part2 = LCD1602-I2C

nets:
  N1: Part1.A0, R1.leg2, R2.Pin_0
  GND: Part1.GND, R2.Pin_1, Part2.GND
  N2: Part1.A4/SDA, Part2.SDA
  N3: Part1.A5/SCL, Part2.SCL
  5V: Part1.5V, R1.wiper, Part2.VCC

custom parts:
  LCD1602-I2C: A standard character display, usually with 2x16 characters. Comes in many colors with LCM1602 IIC attached.
